// Logisim project control-logic.circ as structural Verilog: 1 circuit, main circuit control_logic
module control_logic (
  input  [31:0] Instruction,
  input  BrEq,
  input  BrLt,
  output PCSel,
  output RegWEn,
  output [2:0] ImmSel,
  output BrUn,
  output ASel,
  output BSel,
  output [3:0] ALUSel,
  output MemWEn,
  output [1:0] WBSel
);

  wire add, add_on, addi, and_5_out, and_6_out, and_7_out, and_8_out, and_10_out, and_12_out, and_tun, andi,
       auipc, B_ON, beq, bge, bgeu, blt, bltu, bne, demultiplexer_6_out0, demultiplexer_6_out1,
       demultiplexer_7_out5, I_IMM_ON, jal, jalr, L_ON, lb, lh, lui, lw, mul, mul_on, mulh, mulh_on, mulhu,
       not_1_out, not_2_out, not_3_out, or_1_out, or_2_out, or_tun, ori, R_ON, S_ON, sb, sh, sll_on, sll_tun,
       slli, slt, slti, sra_on, sra_tun, srai, srai_on, srl_on, srl_sra_tun, srl_tun, srli, srli_on, sub,
       sub_on, sw, xor_tun, xori;
  wire [2:0] B_Func3, I_Imm_Func3, L_Func3, R_Func3, S_Func3;
  wire [5:0] priority_encoder_1_out;
  wire [6:0] I_Imm_Funct7, R_Funct7;
  wire [15:14] rom_1_data;
  wire [24:0] demultiplexer_4_out1, demultiplexer_5_out1;
  wire [31:0] demultiplexer_1_out1, demultiplexer_2_out1, demultiplexer_3_out1;

  Comparator #(.width(7)) comparator_1 (.a(Instruction[6:0]), .b(7'b0000011), .eq(L_ON));  // open: gt, lt
  Comparator #(.width(7)) comparator_2 (.a(Instruction[6:0]), .b(7'b0110011), .eq(R_ON));  // open: gt, lt
  Comparator #(.width(7)) comparator_3 (.a(Instruction[6:0]), .b(7'b0010111), .eq(auipc));  // open: gt, lt
  Comparator #(.width(7)) comparator_4 (.a(Instruction[6:0]), .b(7'b0110111), .eq(lui));  // open: gt, lt
  Comparator #(.width(7)) comparator_5 (.a(Instruction[6:0]), .b(7'b1100111), .eq(jalr));  // open: gt, lt
  Comparator #(.width(7)) comparator_6 (.a(Instruction[6:0]), .b(7'b1101111), .eq(jal));  // open: gt, lt
  Priority_Encoder #(.select_enc(6)) priority_encoder_1 (
    .in0(add), .in1(mul), .in2(sub), .in3(sll_tun), .in4(mulh), .in5(mulhu), .in6(slt), .in7(xor_tun),
    .in8(srl_tun), .in9(sra_tun), .in10(or_tun), .in11(and_tun), .in12(lb), .in13(lh), .in14(lw),
    .in15(addi), .in16(slli), .in17(slti), .in18(xori), .in19(srli), .in20(srai), .in21(ori), .in22(andi),
    .in23(sb), .in24(sh), .in25(sw), .in26(beq), .in27(bne), .in28(blt), .in29(bge), .in30(bltu),
    .in31(bgeu), .in32(auipc), .in33(lui), .in34(jal), .in35(jalr), .out(priority_encoder_1_out));  // open: in36, in37, in38, in39, in40, in41, in42, in43, in44, in45, in46, in47, in48, in49, in50, in51, in52, in53, in54, in55, in56, in57, in58, in59, in60, in61, in62, in63, gs, en_out, en_in
  Comparator #(.width(7)) comparator_7 (.a(Instruction[6:0]), .b(7'b0010011), .eq(I_IMM_ON));  // open: gt, lt
  Comparator #(.width(7)) comparator_8 (.a(Instruction[6:0]), .b(7'b1100011), .eq(B_ON));  // open: gt, lt
  Comparator #(.width(7)) comparator_9 (.a(Instruction[6:0]), .b(7'b0100011), .eq(S_ON));  // open: gt, lt
  ROM #(.addrWidth(6), .dataWidth(16)) rom_1 (
    .addr(priority_encoder_1_out),
    .data({rom_1_data, WBSel, MemWEn, ALUSel, BSel, ASel, BrUn, ImmSel, RegWEn}));
  Demultiplexer #(.width(32)) demultiplexer_1 (
    .out1({demultiplexer_1_out1[31:15], B_Func3, demultiplexer_1_out1[11:0]}), .in(Instruction), .sel(B_ON));  // open: out0
  Demultiplexer #(.width(32)) demultiplexer_2 (
    .out1({demultiplexer_2_out1[31:15], L_Func3, demultiplexer_2_out1[11:0]}), .in(Instruction), .sel(L_ON));  // open: out0
  Demultiplexer #(.width(32)) demultiplexer_3 (
    .out1({demultiplexer_3_out1[31:15], S_Func3, demultiplexer_3_out1[11:0]}), .in(Instruction), .sel(S_ON));  // open: out0
  Demultiplexer #(.width(32)) demultiplexer_4 (
    .out1({R_Funct7, demultiplexer_4_out1[24:15], R_Func3, demultiplexer_4_out1[11:0]}), .in(Instruction),
    .sel(R_ON));  // open: out0
  Demultiplexer #(.width(32)) demultiplexer_5 (
    .out1({I_Imm_Funct7, demultiplexer_5_out1[24:15], I_Imm_Func3, demultiplexer_5_out1[11:0]}),
    .in(Instruction), .sel(I_IMM_ON));  // open: out0
  and and_1 (add, add_on, demultiplexer_6_out0);
  Demultiplexer #(.select(3)) demultiplexer_6 (
    .out0(demultiplexer_6_out0), .out1(demultiplexer_6_out1), .out2(slt), .out3(mulhu), .out4(xor_tun),
    .out5(srl_sra_tun), .out6(or_tun), .out7(and_tun), .in(R_ON), .sel(R_Func3));
  Comparator #(.width(7)) comparator_10 (.a(R_Funct7), .b({7{1'b0}}), .eq(add_on));  // open: gt, lt
  Comparator #(.width(7)) comparator_11 (.a(R_Funct7), .b(7'b0100000), .eq(sub_on));  // open: gt, lt
  Comparator #(.width(7)) comparator_12 (.a(R_Funct7), .b(7'b0000001), .eq(mul_on));  // open: gt, lt
  Demultiplexer #(.select(3)) demultiplexer_7 (
    .out0(addi), .out1(slli), .out2(slti), .out4(xori), .out5(demultiplexer_7_out5), .out6(ori), .out7(andi),
    .in(I_IMM_ON), .sel(I_Imm_Func3));  // open: out3
  Comparator #(.width(7)) comparator_13 (.a(I_Imm_Funct7), .b({7{1'b0}}), .eq(srai_on));  // open: gt, lt
  Comparator #(.width(7)) comparator_14 (.a(I_Imm_Funct7), .b(7'b0100000), .eq(srli_on));  // open: gt, lt
  and and_2 (sub, sub_on, demultiplexer_6_out0);
  not not_1 (not_1_out, BrLt);
  and and_3 (srai, srai_on, demultiplexer_7_out5);
  and and_4 (mul, mul_on, demultiplexer_6_out0);
  Comparator #(.width(7)) comparator_15 (.a(R_Funct7), .b({7{1'b0}}), .eq(sll_on));  // open: gt, lt
  Comparator #(.width(7)) comparator_16 (.a(R_Funct7), .b(7'b0000001), .eq(mulh_on));  // open: gt, lt
  and and_5 (and_5_out, beq, BrEq);
  not not_2 (not_2_out, BrEq);
  and and_6 (and_6_out, blt, BrLt);
  and and_7 (and_7_out, bltu, BrLt);
  and and_8 (and_8_out, bge, not_1_out);
  and and_9 (srli, srli_on, demultiplexer_7_out5);
  and and_10 (and_10_out, bne, not_2_out);
  not not_3 (not_3_out, BrLt);
  and and_11 (sll_tun, sll_on, demultiplexer_6_out1);
  and and_12 (and_12_out, bgeu, not_3_out);
  and and_13 (mulh, mulh_on, demultiplexer_6_out1);
  Comparator #(.width(7)) comparator_17 (.a(R_Funct7), .b({7{1'b0}}), .eq(srl_on));  // open: gt, lt
  Comparator #(.width(7)) comparator_18 (.a(R_Funct7), .b(7'b0100000), .eq(sra_on));  // open: gt, lt
  Demultiplexer #(.select(3)) demultiplexer_8 (
    .out0(beq), .out1(bne), .out4(blt), .out5(bge), .out6(bltu), .out7(bgeu), .in(B_ON), .sel(B_Func3));  // open: out2, out3
  and and_14 (srl_tun, srl_sra_tun, srl_on);
  and and_15 (sra_tun, srl_sra_tun, sra_on);
  or or_1 (or_1_out, and_5_out, and_10_out, and_6_out, and_7_out, and_8_out, and_12_out);
  or or_2 (or_2_out, jal, jalr);
  or or_3 (PCSel, or_1_out, or_2_out);
  Demultiplexer #(.select(3)) demultiplexer_9 (
    .out0(lb), .out1(lh), .out2(lw), .in(L_ON), .sel(L_Func3));  // open: out3, out4, out5, out6, out7
  Demultiplexer #(.select(3)) demultiplexer_10 (
    .out0(sb), .out1(sh), .out2(sw), .in(S_ON), .sel(S_Func3));  // open: out3, out4, out5, out6, out7

  // Notes on the sheet:
  //   INPUTS to your circuit
  //   contents of rom_1 (hex, n*v repeats v):
  //   100f 140f 160f 108f 148f 158f 110f 120f 128f 168f 130f 138f 41 41 41 1041 10c1 1141 1341 12c1 16c1
  //   1341 13c1 3842 3842 3842 4*3064 3074 3074 1067 17c7 2069 2041 2041
  //   ROM FOR CONTROL LOGIC
  //   DON'T CHANGE THE LOCATIONS OF THE INPUTS AND OUTPUTS!
  //   This is only if you choose to do the ROM option
  //   OUTPUT from your circuit
  //   Reminder: If using ROM, use combinational logic for PCSel
endmodule
