// Logisim project cpu.circ as structural Verilog: 1 circuit, main circuit cpu
module cpu (
  input  clk,
  input  [31:0] Instruction,
  input  [31:0] MemReadData,
  output [31:0] MemAddress,
  output [31:0] ProgramCounter,
  output [31:0] ra,
  output [31:0] sp,
  output [31:0] t0,
  output [31:0] t1,
  output [31:0] t2,
  output [31:0] s0,
  output [31:0] s1,
  output [31:0] a0,
  output [3:0] MemWriteMask,
  output [31:0] MemWriteData
);

  wire ASel, BrEq, BrLt, BrUn, BSel, MemWEn, PCSel, RegWEn;
  wire [1:0] WBSel;
  wire [2:0] ImmSel;
  wire [3:0] ALUSel;
  wire [31:0] A_input, adder_1_out, adder_2_out, B_input, ex_instr, ex_pc, imm, mem, multiplexer_1_out,
       multiplexer_2_out, RegReadData1, RegReadData2, WriteReg;

  Adder #(.width(32)) adder_1 (.a(ProgramCounter), .b(32'h4), .out(adder_1_out));  // open: cin, cout
  Multiplexer #(.enable("false"), .width(32)) multiplexer_1 (
    .in0(adder_1_out), .in1(MemAddress), .out(multiplexer_1_out), .sel(PCSel));
  Register #(.width(32)) PC (.D(multiplexer_1_out), .clk(clk), .Q(ProgramCounter));  // open: en, clr
  Register #(.width(32)) register_1 (.D(ProgramCounter), .clk(clk), .Q(ex_pc));  // open: en, clr
  Register #(.width(32)) register_2 (.D(multiplexer_2_out), .clk(clk), .Q(ex_instr));  // open: en, clr
  Multiplexer #(.enable("false"), .width(32)) multiplexer_2 (
    .in0(Instruction), .in1(32'h13), .out(multiplexer_2_out), .sel(PCSel));
  control_logic control_logic_1 (
    .Instruction(ex_instr), .BrEq(BrEq), .BrLt(BrLt), .PCSel(PCSel), .RegWEn(RegWEn), .ImmSel(ImmSel),
    .BrUn(BrUn), .ASel(ASel), .BSel(BSel), .ALUSel(ALUSel), .MemWEn(MemWEn), .WBSel(WBSel));
  regfile regfile_1 (
    .rs1(ex_instr[19:15]), .rs2(ex_instr[24:20]), .rd(ex_instr[11:7]), .Write_Data(WriteReg),
    .RegWEn(RegWEn), .clk(clk), .ra(ra), .sp(sp), .t0(t0), .t1(t1), .t2(t2), .s0(s0), .s1(s1), .a0(a0),
    .Read_Data_1(RegReadData1), .Read_Data_2(RegReadData2));
  imm_gen imm_gen_1 (.Instruction(ex_instr), .ImmSel(ImmSel), .Immediate(imm));
  alu alu_1 (.A(A_input), .B(B_input), .ALUSel(ALUSel), .ALUResult(MemAddress));
  branch_comp branch_comp_1 (.BrData1(RegReadData1), .BrData2(RegReadData2), .BrUn(BrUn), .BrEq(BrEq), .BrLt(BrLt));
  Multiplexer #(.enable("false"), .width(32)) multiplexer_3 (.in0(RegReadData2), .in1(imm), .out(B_input), .sel(BSel));
  Multiplexer #(.enable("false"), .width(32)) multiplexer_4 (
    .in0(RegReadData1), .in1(ex_pc), .out(A_input), .sel(ASel));
  partial_store partial_store_1 (
    .Instruction(ex_instr), .MemAddress(MemAddress), .DataFromReg(RegReadData2), .MemWEn(MemWEn),
    .MemWriteMask(MemWriteMask), .DataToMem(MemWriteData));
  partial_load partial_load_1 (
    .Instruction(ex_instr), .MemAddress(MemAddress), .DataFromMem(MemReadData), .DataToReg(mem));
  Adder #(.width(32)) adder_2 (.a(ex_pc), .b(32'h4), .out(adder_2_out));  // open: cin, cout
  Multiplexer #(.enable("false"), .select(2), .width(32)) multiplexer_5 (
    .in0(adder_2_out), .in1(MemAddress), .in2(mem), .out(WriteReg), .sel(WBSel));  // open: in3

  // Other names for the same wires on the sheet: ALURes[31:0] = MemAddress; opcode[6:0] = ex_instr[6:0];
  //   rd[4:0] = ex_instr[11:7]; funct3[2:0] = ex_instr[14:12]; rs1[4:0] = ex_instr[19:15]; rs2[4:0] = ex_instr[24:20];
  //   funct7[6:0] = ex_instr[31:25]

  // Notes on the sheet:
  //   To IMEM
  //   IMEM (do **NOT** move this)
  //   From IMEM
  //   Inputs/Outputs for testing. Do **NOT** move these.
  //   To DMEM
  //   DMEM (do **NOT** move this)
  //   From DMEM
endmodule
