// Logisim project partial-load.circ as structural Verilog: 1 circuit, main circuit partial_load
module partial_load (
  input  [31:0] Instruction,
  input  [31:0] MemAddress,
  input  [31:0] DataFromMem,
  output [31:0] DataToReg
);

  wire [7:0] undriven, undriven_2, undriven_3, undriven_4;
  wire [31:0] bit_extender_1_out, bit_extender_2_out, bit_extender_3_out, bit_extender_4_out,
       bit_extender_5_out, bit_extender_6_out, bit_extender_7_out, multiplexer_1_out, multiplexer_2_out;

  assign bit_extender_1_out = {{24{undriven[7]}}, undriven};  // Bit_Extender bit_extender_1
  assign bit_extender_2_out = {{24{undriven_2[7]}}, undriven_2};  // Bit_Extender bit_extender_2
  assign bit_extender_3_out = {{24{undriven_3[7]}}, undriven_3};  // Bit_Extender bit_extender_3
  assign bit_extender_4_out = {{24{undriven_4[7]}}, undriven_4};  // Bit_Extender bit_extender_4
  assign bit_extender_5_out = {{16{undriven_2[7]}}, {undriven_2, undriven}};  // Bit_Extender bit_extender_5
  assign bit_extender_6_out = {{16{undriven_3[7]}}, {undriven_3, undriven_2}};  // Bit_Extender bit_extender_6
  assign bit_extender_7_out = {{16{undriven_4[7]}}, {undriven_4, undriven_3}};  // Bit_Extender bit_extender_7
  Multiplexer #(.select(2), .width(32)) multiplexer_1 (
    .in0(bit_extender_5_out), .in1(bit_extender_6_out), .in2(bit_extender_7_out), .out(multiplexer_1_out),
    .sel(MemAddress[1:0]));  // open: in3
  Multiplexer #(.select(2), .width(32)) multiplexer_2 (
    .in0(bit_extender_1_out), .in1(bit_extender_2_out), .in2(bit_extender_3_out), .in3(bit_extender_4_out),
    .out(multiplexer_2_out), .sel(MemAddress[1:0]));
  Multiplexer #(.select(3), .width(32)) multiplexer_3 (
    .in0(multiplexer_2_out), .in1(multiplexer_1_out), .in2({undriven_4, undriven_3, undriven_2, undriven}),
    .in3(DataToReg), .in4(DataToReg), .in5(DataToReg), .in6(DataToReg), .in7(DataToReg), .out(DataToReg),
    .sel(Instruction[14:12]));

  // Other names for the same wires on the sheet: funct_3[2:0] = Instruction[14:12]; bot_bits[1:0] = MemAddress[1:0]

  // Notes on the sheet:
  //   INPUTS to your circuit
  //   DON'T CHANGE THE LOCATIONS OF THE INPUTS AND OUTPUTS!
  //   OUTPUT from your circuit
endmodule
